# Fritzing sketch MelodyModule_Schematic (saved by Fritzing 0.8.3b)
breadboards: 1

parts:
  IC1 = attiny85 [package=dip]
  Piezo = Piezo Speaker
  VCC1_coincell = Battery
  R2 = Resistor [tolerance=±5% resistance=10k package=THT]
  Reed_1 = Reed switch [package=THT]
  Out_Headers = male pin header, 3 pins [form="♂ (male)"]
  S2_slide = Square Pushbutton
  R3_trimpot = Trimmer Potentiometer [maximum_resistance=10kΩ package=THT]

nets:
  N1: IC1.Pin_1, Piezo.pin2
  N2: IC1.Pin_4, Reed_1.pin_1, Out_Headers.pin1, S2_slide.leg0
  N3: IC1.Pin_6, R2.Pin_1
  N4: IC1.Pin_8, VCC1_coincell.-, R3_trimpot.leg2
  N5: Piezo.pin1, R3_trimpot.wiper
  GND: Out_Headers.pin3

notes:
  Reusable Melody Module
  An ATtiny85 board
  2014-02-25 Ando Roots <ando@sqroot.eu>
  The board operates from a coincell battery (3V) and plays a melody (piezo) when the trigger (pin 1) is HIGH. Can be triggered via a reed switch or with the output headers from an external source. The IC is in a socket and reprogrammable.
